// Logisim project COMPARATORS.circ as structural Verilog: 3 circuits, main circuit Half_Comparator(1)
module Half_Comparator_1 (
  input  A,
  input  B,
  output EQ
);

  xnor xnor_1 (EQ, A, B);
endmodule

module Full_Comparator_1 (
  input  A,
  input  B,
  input  EQ_IN,
  output EQ
);

  wire xnor_1_out;

  xnor xnor_1 (xnor_1_out, B, A);
  and and_1 (EQ, xnor_1_out, EQ_IN);
endmodule

module _20Bit_Comparator_1 (
  input  [19:0] in_1,
  input  [19:0] in_2,
  output EQ
);

  wire full_comparator_1_1_eq, full_comparator_1_2_eq, full_comparator_1_3_eq, full_comparator_1_4_eq,
       full_comparator_1_5_eq, full_comparator_1_6_eq, full_comparator_1_7_eq, full_comparator_1_8_eq,
       full_comparator_1_9_eq, full_comparator_1_10_eq, full_comparator_1_11_eq, full_comparator_1_12_eq,
       full_comparator_1_13_eq, full_comparator_1_14_eq, full_comparator_1_15_eq, full_comparator_1_16_eq,
       full_comparator_1_17_eq, full_comparator_1_18_eq, half_comparator_1_1_eq;

  Half_Comparator_1 half_comparator_1_1 (.A(in_1[19]), .EQ(half_comparator_1_1_eq), .B(in_2[19]));
  Full_Comparator_1 full_comparator_1_1 (
    .A(in_1[18]), .EQ_IN(half_comparator_1_1_eq), .EQ(full_comparator_1_1_eq), .B(in_2[18]));
  Full_Comparator_1 full_comparator_1_2 (
    .A(in_1[17]), .EQ_IN(full_comparator_1_1_eq), .EQ(full_comparator_1_2_eq), .B(in_2[17]));
  Full_Comparator_1 full_comparator_1_3 (
    .A(in_1[16]), .EQ_IN(full_comparator_1_2_eq), .EQ(full_comparator_1_3_eq), .B(in_2[16]));
  Full_Comparator_1 full_comparator_1_4 (
    .A(in_1[15]), .EQ_IN(full_comparator_1_3_eq), .EQ(full_comparator_1_4_eq), .B(in_2[15]));
  Full_Comparator_1 full_comparator_1_5 (
    .A(in_1[14]), .EQ_IN(full_comparator_1_4_eq), .EQ(full_comparator_1_5_eq), .B(in_2[14]));
  Full_Comparator_1 full_comparator_1_6 (
    .A(in_1[13]), .EQ_IN(full_comparator_1_5_eq), .EQ(full_comparator_1_6_eq), .B(in_2[13]));
  Full_Comparator_1 full_comparator_1_7 (
    .A(in_1[12]), .EQ_IN(full_comparator_1_6_eq), .EQ(full_comparator_1_7_eq), .B(in_2[12]));
  Full_Comparator_1 full_comparator_1_8 (
    .A(in_1[11]), .EQ_IN(full_comparator_1_7_eq), .EQ(full_comparator_1_8_eq), .B(in_2[11]));
  Full_Comparator_1 full_comparator_1_9 (
    .A(in_1[10]), .EQ_IN(full_comparator_1_8_eq), .EQ(full_comparator_1_9_eq), .B(in_2[10]));
  Full_Comparator_1 full_comparator_1_10 (
    .A(in_1[9]), .EQ_IN(full_comparator_1_9_eq), .EQ(full_comparator_1_10_eq), .B(in_2[9]));
  Full_Comparator_1 full_comparator_1_11 (
    .A(in_1[8]), .EQ_IN(full_comparator_1_10_eq), .EQ(full_comparator_1_11_eq), .B(in_2[8]));
  Full_Comparator_1 full_comparator_1_12 (
    .A(in_1[7]), .EQ_IN(full_comparator_1_11_eq), .EQ(full_comparator_1_12_eq), .B(in_2[7]));
  Full_Comparator_1 full_comparator_1_13 (
    .A(in_1[6]), .EQ_IN(full_comparator_1_12_eq), .EQ(full_comparator_1_13_eq), .B(in_2[6]));
  Full_Comparator_1 full_comparator_1_14 (
    .A(in_1[5]), .EQ_IN(full_comparator_1_13_eq), .EQ(full_comparator_1_14_eq), .B(in_2[5]));
  Full_Comparator_1 full_comparator_1_15 (
    .A(in_1[4]), .EQ_IN(full_comparator_1_14_eq), .EQ(full_comparator_1_15_eq), .B(in_2[4]));
  Full_Comparator_1 full_comparator_1_16 (
    .A(in_1[3]), .EQ_IN(full_comparator_1_15_eq), .EQ(full_comparator_1_16_eq), .B(in_2[3]));
  Full_Comparator_1 full_comparator_1_17 (
    .A(in_1[2]), .EQ_IN(full_comparator_1_16_eq), .EQ(full_comparator_1_17_eq), .B(in_2[2]));
  Full_Comparator_1 full_comparator_1_18 (
    .A(in_1[1]), .EQ_IN(full_comparator_1_17_eq), .EQ(full_comparator_1_18_eq), .B(in_2[1]));
  Full_Comparator_1 full_comparator_1_19 (.A(in_1[0]), .EQ_IN(full_comparator_1_18_eq), .EQ(EQ), .B(in_2[0]));
endmodule
