// Logisim project MAIN.circ as structural Verilog: 9 circuits, main circuit Register_File(1)
module Register_File_1 (
  input  Load,
  input  [19:0] in_2,
  input  Clk,
  input  [3:0] wr,
  input  [3:0] rd1,
  input  [3:0] rd2,
  output [19:0] outData1,
  output [19:0] outData2
);

  wire and_1_out, and_2_out, and_3_out, and_4_out, and_5_out, and_6_out, and_7_out, and_8_out, and_9_out,
       and_10_out, and_11_out, and_12_out, and_13_out, and_14_out, and_15_out, and_16_out, decoder_1_out0,
       decoder_1_out1, decoder_1_out2, decoder_1_out3, decoder_1_out4, decoder_1_out5, decoder_1_out6,
       decoder_1_out7, decoder_1_out8, decoder_1_out9, decoder_1_out10, decoder_1_out11, decoder_1_out12,
       decoder_1_out13, decoder_1_out14, decoder_1_out15, decoder_2_out0, decoder_2_out1, decoder_2_out2,
       decoder_2_out3, decoder_2_out4, decoder_2_out5, decoder_2_out6, decoder_2_out7, decoder_2_out8,
       decoder_2_out9, decoder_2_out10, decoder_2_out11, decoder_2_out12, decoder_2_out13, decoder_2_out14,
       decoder_2_out15, decoder_3_out0, decoder_3_out1, decoder_3_out2, decoder_3_out3, decoder_3_out4,
       decoder_3_out5, decoder_3_out6, decoder_3_out7, decoder_3_out8, decoder_3_out9, decoder_3_out10,
       decoder_3_out11, decoder_3_out12, decoder_3_out13, decoder_3_out14, decoder_3_out15;
  wire [19:0] R0_q, R1_q, R2_q, R3_q, R4_q, R5_q, R6_q, R7_q, R8_q, R9_q, R10_q, R11_q, R12_q, R13_q, R14_q,
       R15_q;

  Decoder #(.select(4), .enable("false")) decoder_1 (
    .out0(decoder_1_out0), .out1(decoder_1_out1), .out2(decoder_1_out2), .out3(decoder_1_out3),
    .out4(decoder_1_out4), .out5(decoder_1_out5), .out6(decoder_1_out6), .out7(decoder_1_out7),
    .out8(decoder_1_out8), .out9(decoder_1_out9), .out10(decoder_1_out10), .out11(decoder_1_out11),
    .out12(decoder_1_out12), .out13(decoder_1_out13), .out14(decoder_1_out14), .out15(decoder_1_out15),
    .sel(wr));
  and and_1 (and_1_out, Load, decoder_1_out0);
  and and_2 (and_2_out, Load, decoder_1_out1);
  and and_3 (and_3_out, Load, decoder_1_out2);
  and and_4 (and_4_out, Load, decoder_1_out3);
  and and_5 (and_5_out, Load, decoder_1_out4);
  and and_6 (and_6_out, Load, decoder_1_out5);
  and and_7 (and_7_out, Load, decoder_1_out6);
  and and_8 (and_8_out, Load, decoder_1_out7);
  Register #(.width(20)) R0 (.D(in_2), .en(and_1_out), .Q(R0_q), .clk(Clk), .clr(1'b0));
  Register #(.width(20)) R1 (.D(in_2), .en(and_2_out), .Q(R1_q), .clk(Clk), .clr(1'b0));
  Register #(.width(20)) R2 (.D(in_2), .en(and_3_out), .Q(R2_q), .clk(Clk), .clr(1'b0));
  Register #(.width(20)) R3 (.D(in_2), .en(and_4_out), .Q(R3_q), .clk(Clk), .clr(1'b0));
  Register #(.width(20)) R4 (.D(in_2), .en(and_5_out), .Q(R4_q), .clk(Clk), .clr(1'b0));
  Register #(.width(20)) R5 (.D(in_2), .en(and_6_out), .Q(R5_q), .clk(Clk), .clr(1'b0));
  Register #(.width(20)) R6 (.D(in_2), .en(and_7_out), .Q(R6_q), .clk(Clk), .clr(1'b0));
  Register #(.width(20)) R7 (.D(in_2), .en(and_8_out), .Q(R7_q), .clk(Clk), .clr(1'b0));
  and and_9 (and_9_out, Load, decoder_1_out8);
  and and_10 (and_10_out, Load, decoder_1_out9);
  and and_11 (and_11_out, Load, decoder_1_out10);
  and and_12 (and_12_out, Load, decoder_1_out11);
  and and_13 (and_13_out, Load, decoder_1_out12);
  and and_14 (and_14_out, Load, decoder_1_out13);
  and and_15 (and_15_out, Load, decoder_1_out14);
  and and_16 (and_16_out, Load, decoder_1_out15);
  Decoder #(.select(4), .enable("false")) decoder_2 (
    .out0(decoder_2_out0), .out1(decoder_2_out1), .out2(decoder_2_out2), .out3(decoder_2_out3),
    .out4(decoder_2_out4), .out5(decoder_2_out5), .out6(decoder_2_out6), .out7(decoder_2_out7),
    .out8(decoder_2_out8), .out9(decoder_2_out9), .out10(decoder_2_out10), .out11(decoder_2_out11),
    .out12(decoder_2_out12), .out13(decoder_2_out13), .out14(decoder_2_out14), .out15(decoder_2_out15),
    .sel(rd1));
  Decoder #(.select(4), .enable("false")) decoder_3 (
    .out0(decoder_3_out0), .out1(decoder_3_out1), .out2(decoder_3_out2), .out3(decoder_3_out3),
    .out4(decoder_3_out4), .out5(decoder_3_out5), .out6(decoder_3_out6), .out7(decoder_3_out7),
    .out8(decoder_3_out8), .out9(decoder_3_out9), .out10(decoder_3_out10), .out11(decoder_3_out11),
    .out12(decoder_3_out12), .out13(decoder_3_out13), .out14(decoder_3_out14), .out15(decoder_3_out15),
    .sel(rd2));
  Register #(.width(20)) R8 (.D(in_2), .en(and_9_out), .Q(R8_q), .clk(Clk), .clr(1'b0));
  Register #(.width(20)) R9 (.D(in_2), .en(and_10_out), .Q(R9_q), .clk(Clk), .clr(1'b0));
  Register #(.width(20)) R10 (.D(in_2), .en(and_11_out), .Q(R10_q), .clk(Clk), .clr(1'b0));
  Register #(.width(20)) R11 (.D(in_2), .en(and_12_out), .Q(R11_q), .clk(Clk), .clr(1'b0));
  Register #(.width(20)) R12 (.D(in_2), .en(and_13_out), .Q(R12_q), .clk(Clk), .clr(1'b0));
  Register #(.width(20)) R13 (.D(in_2), .en(and_14_out), .Q(R13_q), .clk(Clk), .clr(1'b0));
  Register #(.width(20)) R14 (.D(in_2), .en(and_15_out), .Q(R14_q), .clk(Clk), .clr(1'b0));
  Register #(.width(20)) R15 (.D(in_2), .en(and_16_out), .Q(R15_q), .clk(Clk), .clr(1'b0));
  assign outData1 = decoder_2_out0 ? R0_q : 20'bz;  // Controlled_Buffer controlled_buffer_1
  assign outData2 = decoder_3_out0 ? R0_q : 20'bz;  // Controlled_Buffer controlled_buffer_2
  assign outData1 = decoder_2_out1 ? R1_q : 20'bz;  // Controlled_Buffer controlled_buffer_3
  assign outData2 = decoder_3_out1 ? R1_q : 20'bz;  // Controlled_Buffer controlled_buffer_4
  assign outData1 = decoder_2_out2 ? R2_q : 20'bz;  // Controlled_Buffer controlled_buffer_5
  assign outData2 = decoder_3_out2 ? R2_q : 20'bz;  // Controlled_Buffer controlled_buffer_6
  assign outData1 = decoder_2_out3 ? R3_q : 20'bz;  // Controlled_Buffer controlled_buffer_7
  assign outData2 = decoder_3_out3 ? R3_q : 20'bz;  // Controlled_Buffer controlled_buffer_8
  assign outData1 = decoder_2_out4 ? R4_q : 20'bz;  // Controlled_Buffer controlled_buffer_9
  assign outData2 = decoder_3_out4 ? R4_q : 20'bz;  // Controlled_Buffer controlled_buffer_10
  assign outData1 = decoder_2_out5 ? R5_q : 20'bz;  // Controlled_Buffer controlled_buffer_11
  assign outData2 = decoder_3_out5 ? R5_q : 20'bz;  // Controlled_Buffer controlled_buffer_12
  assign outData1 = decoder_2_out6 ? R6_q : 20'bz;  // Controlled_Buffer controlled_buffer_13
  assign outData2 = decoder_3_out6 ? R6_q : 20'bz;  // Controlled_Buffer controlled_buffer_14
  assign outData1 = decoder_2_out7 ? R7_q : 20'bz;  // Controlled_Buffer controlled_buffer_15
  assign outData2 = decoder_3_out7 ? R7_q : 20'bz;  // Controlled_Buffer controlled_buffer_16
  assign outData1 = decoder_2_out8 ? R8_q : 20'bz;  // Controlled_Buffer controlled_buffer_17
  assign outData2 = decoder_3_out8 ? R8_q : 20'bz;  // Controlled_Buffer controlled_buffer_18
  assign outData1 = decoder_2_out9 ? R9_q : 20'bz;  // Controlled_Buffer controlled_buffer_19
  assign outData2 = decoder_3_out9 ? R9_q : 20'bz;  // Controlled_Buffer controlled_buffer_20
  assign outData1 = decoder_2_out10 ? R10_q : 20'bz;  // Controlled_Buffer controlled_buffer_21
  assign outData2 = decoder_3_out10 ? R10_q : 20'bz;  // Controlled_Buffer controlled_buffer_22
  assign outData1 = decoder_2_out11 ? R11_q : 20'bz;  // Controlled_Buffer controlled_buffer_23
  assign outData2 = decoder_3_out11 ? R11_q : 20'bz;  // Controlled_Buffer controlled_buffer_24
  assign outData1 = decoder_2_out12 ? R12_q : 20'bz;  // Controlled_Buffer controlled_buffer_25
  assign outData2 = decoder_3_out12 ? R12_q : 20'bz;  // Controlled_Buffer controlled_buffer_26
  assign outData1 = decoder_2_out13 ? R13_q : 20'bz;  // Controlled_Buffer controlled_buffer_27
  assign outData2 = decoder_3_out13 ? R13_q : 20'bz;  // Controlled_Buffer controlled_buffer_28
  assign outData1 = decoder_2_out14 ? R14_q : 20'bz;  // Controlled_Buffer controlled_buffer_29
  assign outData2 = decoder_3_out14 ? R14_q : 20'bz;  // Controlled_Buffer controlled_buffer_30
  assign outData1 = decoder_2_out15 ? R15_q : 20'bz;  // Controlled_Buffer controlled_buffer_31
  assign outData2 = decoder_3_out15 ? R15_q : 20'bz;  // Controlled_Buffer controlled_buffer_32
endmodule

module ALU_1 (
  input  [19:0] Input_1,
  input  [19:0] Input_2,
  input  [2:0] ALU_Controller,
  output [19:0] ALU_Out
);

  wire not_1_out;
  wire [19:0] Add_Sub_sum, and_1_out, or_1_out, xor_1_out;

  not not_1 (not_1_out, ALU_Controller[1]);
  assign and_1_out = Input_1 & Input_2;  // AND_Gate and_1, 20 bits wide
  Adder___20_Bits Add_Sub (
    .Input_1(Input_1), .sub_1_add_0(not_1_out), .Input_2(Input_2), .SUM(Add_Sub_sum));  // open: Overflow
  assign or_1_out = Input_1 | Input_2;  // OR_Gate or_1, 20 bits wide
  assign xor_1_out = Input_1 ^ Input_2;  // XOR_Gate xor_1, 20 bits wide
  Multiplexer #(.select(3), .width(20), .enable("false")) multiplexer_1 (
    .in0(and_1_out), .in1(Add_Sub_sum), .in2(or_1_out), .in3(Add_Sub_sum), .in4(xor_1_out), .out(ALU_Out),
    .sel(ALU_Controller));  // open: in5, in6, in7
endmodule

// INST PARSER
module Instruction_Parser_1 (
  input  [19:0] Instruction,
  output [19:0] Address7,
  output [3:0] SR2,
  output Z,
  output [2:0] ALU_Bits,
  output [3:0] Destination_Register,
  output [9:0] Address12,
  output [3:0] Source_Register,
  output [3:0] SR1,
  output [19:0] Imm
);

  wire and_1_out;

  assign Address7 = {{13{Instruction[7]}}, Instruction[7:1]};  // Bit_Extender bit_extender_1
  assign Imm = {{12{Instruction[7]}}, Instruction[7:0]};  // Bit_Extender bit_extender_2
  and and_1 (and_1_out, Instruction[19], Instruction[18], Instruction[17], Instruction[16]);
  and and_2 (Z, Instruction[0], and_1_out);

  assign Address12 = Instruction[9:0];
  assign ALU_Bits = Instruction[19:17];
  assign Destination_Register = Instruction[15:12];
  assign Source_Register = Instruction[15:12];
  assign SR1 = Instruction[11:8];
  assign SR2 = Instruction[7:4];

  // Other names for the same wires on the sheet: Opcode[3:0] = Instruction[19:16]
endmodule

module Program_Counter_1 (
  input  [19:0] JUMP_ADDRESS,
  input  Clear,
  input  Enable,
  input  Clock,
  input  ADDRSelect,
  output [9:0] PC_address
);

  wire [19:0] adder_20_bits_1_sum, multiplexer_1_out, multiplexer_2_out;
  wire [19:10] register_1_q;

  Multiplexer #(.width(20)) multiplexer_1 (
    .in0(20'h1), .in1(JUMP_ADDRESS), .out(multiplexer_1_out), .sel(ADDRSelect));  // open: en
  Adder___20_Bits adder_20_bits_1 (
    .Input_1(multiplexer_1_out), .sub_1_add_0(1'b0), .Input_2(multiplexer_2_out), .SUM(adder_20_bits_1_sum));  // open: Overflow
  Multiplexer #(.width(20)) multiplexer_2 (
    .in0({register_1_q, PC_address}), .in1({20{1'b0}}), .out(multiplexer_2_out), .sel(ADDRSelect));  // open: en
  Register #(.width(20), .trigger("falling")) register_1 (
    .D(adder_20_bits_1_sum), .en(Enable), .Q({register_1_q, PC_address}), .clk(Clock), .clr(Clear));
endmodule

module Sign_Extend_Value_1 (
  input  [19:0] Input,
  output [19:0] Output
);


  assign Output = {{5{Input[15]}}, Input[14:0]};
endmodule

module Branch_Signal_1 (
  input  [19:0] input1,
  input  [19:0] input2,
  input  z,
  output out_4
);

  wire n20bit_comparator_1_1_eq, not_1_out;

  _20Bit_Comparator_1 u_20bit_comparator_1_1 (.in_1(input1), .in_2(input2), .EQ(n20bit_comparator_1_1_eq));
  not not_1 (not_1_out, n20bit_comparator_1_1_eq);
  Multiplexer #(.enable("false")) multiplexer_1 (.in0(not_1_out), .in1(n20bit_comparator_1_1_eq), .out(out_4), .sel(z));
endmodule

// CONTROL UNIT
module Control_Unit__1 (
  input  [19:0] Instruction,
  input  in_2,
  input  in_3,
  output ALU_Signal,
  output Immediate_Signal,
  output Memory_Write,
  output JumpDecider,
  output SP_Stack_Add,
  output Memory_Read,
  output Push_Signal,
  output Reg_Write,
  output Pop_Signal,
  output Branch_Signal,
  output PCWrite,
  output PCRead,
  output InstrRead
);

  wire and_2_out, and_3_out, and_5_out, and_6_out, and_13_out, and_15_out, decoder_2_out0, decoder_2_out1,
       decoder_2_out2, decoder_2_out3, decoder_2_out4, decoder_2_out5, decoder_2_out6, decoder_2_out7,
       decoder_2_out8, decoder_2_out9, decoder_2_out10, decoder_2_out11, decoder_2_out12, decoder_2_out13,
       decoder_2_out14, decoder_2_out15, JumpState1, not_1_out, or_2_out, or_3_out, or_5_out, or_6_out,
       or_7_out, State3, State4;
  wire [1:0] counter_1_q;

  and and_1 (JumpState1, Memory_Write, State3);
  Counter #(.width(2), .max('h3)) counter_1 (
    .load(JumpState1), .D(2'b11), .count(not_1_out), .Q(counter_1_q), .clk(in_2), .clr(in_3));  // open: carry
  not not_1 (not_1_out, JumpState1);
  and and_2 (and_2_out, State4, decoder_2_out13);
  and and_3 (and_3_out, State3, decoder_2_out14);
  or or_1 (SP_Stack_Add, and_2_out, and_3_out);
  and and_4 (Pop_Signal, decoder_2_out14, State4);
  Decoder #(.select(2)) decoder_1 (
    .out0(PCRead), .out1(InstrRead), .out2(State3), .out3(State4), .sel(counter_1_q));  // open: en
  Decoder #(.select(4), .enable("false")) decoder_2 (
    .out0(decoder_2_out0), .out1(decoder_2_out1), .out2(decoder_2_out2), .out3(decoder_2_out3),
    .out4(decoder_2_out4), .out5(decoder_2_out5), .out6(decoder_2_out6), .out7(decoder_2_out7),
    .out8(decoder_2_out8), .out9(decoder_2_out9), .out10(decoder_2_out10), .out11(decoder_2_out11),
    .out12(decoder_2_out12), .out13(decoder_2_out13), .out14(decoder_2_out14), .out15(decoder_2_out15),
    .sel(Instruction[19:16]));
  or or_2 (or_2_out, decoder_2_out11, decoder_2_out14);
  or or_3 (or_3_out, decoder_2_out15, decoder_2_out10);
  and and_5 (and_5_out, State3, decoder_2_out12);
  and and_6 (and_6_out, State4, decoder_2_out13);
  and and_7 (JumpDecider, State3, decoder_2_out10);
  and and_8 (Memory_Read, State3, or_2_out);
  and and_9 (Branch_Signal, State3, decoder_2_out15);
  or or_4 (Memory_Write, and_5_out, and_6_out);
  and and_10 (PCWrite, State4, or_3_out);
  or or_5 (or_5_out, decoder_2_out0, decoder_2_out2, decoder_2_out4, decoder_2_out6, decoder_2_out8);
  or or_6 (or_6_out, decoder_2_out1, decoder_2_out3, decoder_2_out5, decoder_2_out7, decoder_2_out9);
  and and_11 (ALU_Signal, or_5_out, State3);
  and and_12 (Immediate_Signal, or_6_out, State3);
  or or_7 (or_7_out, or_5_out, or_6_out, decoder_2_out11);
  and and_13 (and_13_out, State4, or_7_out);
  and and_14 (Push_Signal, State3, decoder_2_out13);
  or or_8 (Reg_Write, and_13_out, and_15_out);
  and and_15 (and_15_out, decoder_2_out14, State4);

  // Other names for the same wires on the sheet: ResetControl = Memory_Write; State1 = PCRead; State2 = InstrRead
endmodule

module CPU__1 (
  input  in_1,
  input  in_2,
  output [19:0] out_3,
  output [9:0] out_4
);

  wire ALU_Signal, and_1_out, and_2_out, and_3_out, BG, Branch_Signal, Clock, comparator_1_eq,
       Immediate_Signal, InstrRead, JumpDecider, Memory_Read, Memory_Write, not_1_out, or_1_out, or_3_out,
       or_4_out, or_5_out, or_6_out, PCRead, PCSelect, PCWrite, PCWriteSignal, Pop_Signal, Push_Signal,
       register_2_q, register_5_q, register_6_q, register_7_q, regWrite, SP_Stack_Addr, Z;
  wire [2:0] ALU_Bits;
  wire [3:0] Destination_Register, multiplexer_4_out, multiplexer_6_out, Source_Register, SR1, SR2;
  wire [9:0] Address12, multiplexer_5_out, PC_Value;
  wire [19:0] adder_20_bits_1_sum, Address7, AluResult, bit_extender_1_out, ExtendJump, Immediate, Instr,
       multiplexer_1_out, multiplexer_2_out, multiplexer_3_out, register_1_q, register_4_q, rom_1_data,
       Source_1, Source_2;

  Control_Unit__1 control_unit_1_1 (
    .Instruction(Instr), .in_2(Clock), .ALU_Signal(ALU_Signal), .Immediate_Signal(Immediate_Signal),
    .Memory_Write(Memory_Write), .JumpDecider(JumpDecider), .Memory_Read(Memory_Read), .Reg_Write(regWrite),
    .Branch_Signal(Branch_Signal), .PCWrite(PCWriteSignal), .PCRead(PCRead), .InstrRead(InstrRead),
    .in_3(in_2), .Push_Signal(Push_Signal), .SP_Stack_Add(SP_Stack_Addr), .Pop_Signal(Pop_Signal));
  Multiplexer #(.width(20), .enable("false")) multiplexer_1 (
    .in0(Immediate), .in1(Source_2), .out(multiplexer_1_out), .sel(ALU_Signal));
  Multiplexer #(.width(20), .enable("false")) multiplexer_2 (
    .in0(ExtendJump), .in1(Address7), .out(multiplexer_2_out), .sel(Branch_Signal));
  Adder___20_Bits adder_20_bits_1 (
    .Input_1(multiplexer_2_out), .sub_1_add_0(1'b0), .Input_2(bit_extender_1_out), .SUM(adder_20_bits_1_sum));  // open: Overflow
  assign bit_extender_1_out = {{10{1'b0}}, PC_Value};  // Bit_Extender bit_extender_1
  Register #(.width(20)) register_1 (
    .D(adder_20_bits_1_sum), .en(PCSelect), .Q(register_1_q), .clk(Clock), .clr(InstrRead));
  Register #(.width(1)) register_2 (.D(PCWrite), .en(PCWrite), .Q(register_2_q), .clk(Clock), .clr(InstrRead));
  Sign_Extend_Value_1 sign_extend_value_1_1 (.Input(Instr), .Output(ExtendJump));
  Clock clock_1 (.out(Clock));
  ALU_1 alu_1_1 (.Input_1(Source_1), .Input_2(multiplexer_1_out), .ALU_Controller(ALU_Bits), .ALU_Out(AluResult));
  Instruction_Parser_1 instruction_parser_1_1 (
    .Instruction(Instr), .ALU_Bits(ALU_Bits), .Address7(Address7), .SR2(SR2), .Z(Z),
    .Destination_Register(Destination_Register), .Address12(Address12), .Source_Register(Source_Register),
    .SR1(SR1), .Imm(Immediate));
  Program_Counter_1 program_counter_1_1 (
    .JUMP_ADDRESS(register_1_q), .ADDRSelect(register_2_q), .PC_address(PC_Value), .Enable(PCRead),
    .Clock(Clock), .Clear(in_2));
  and and_1 (and_1_out, BG, Branch_Signal);
  or or_1 (or_1_out, Memory_Read, Immediate_Signal, ALU_Signal);
  Branch_Signal_1 branch_signal_1_1 (.input1(Source_1), .input2(Source_2), .z(Z), .out_4(BG));
  or or_2 (PCSelect, JumpDecider, and_1_out);
  ROM #(.addrWidth(10), .dataWidth(20)) rom_1 (.addr(PC_Value), .data(rom_1_data), .sel(1'b1));
  Multiplexer #(.width(20), .enable("false")) multiplexer_3 (
    .in0(out_3), .in1(AluResult), .out(multiplexer_3_out), .sel(or_3_out));
  or or_3 (or_3_out, ALU_Signal, Immediate_Signal);
  Register #(.width(20)) register_3 (.D(rom_1_data), .en(InstrRead), .Q(Instr), .clk(Clock), .clr(in_2));
  Register #(.width(20)) register_4 (.D(multiplexer_3_out), .en(or_1_out), .Q(register_4_q), .clk(Clock), .clr(in_2));
  Multiplexer #(.width(4), .enable("false")) multiplexer_4 (
    .in0(Source_Register), .in1(SR1), .out(multiplexer_4_out), .sel(or_4_out));
  or or_4 (or_4_out, ALU_Signal, Immediate_Signal);
  not not_1 (not_1_out, Pop_Signal);
  Multiplexer #(.width(10), .enable("false")) multiplexer_5 (
    .in0(Address12), .in1(out_4), .out(multiplexer_5_out), .sel(SP_Stack_Addr));
  Multiplexer #(.width(4), .enable("false")) multiplexer_6 (
    .in0(SR2), .in1(SR1), .out(multiplexer_6_out), .sel(Branch_Signal));
  or or_5 (or_5_out, not_1_out, Push_Signal);
  or or_6 (or_6_out, Push_Signal, Pop_Signal, comparator_1_eq);
  RAM #(.addrWidth(10), .dataWidth(20), .bus("separate")) ram_1 (
    .addr(multiplexer_5_out), .din(Source_1), .data(out_3), .str(Memory_Write), .sel(1'b1), .clk(Clock),
    .ld(Memory_Read), .clr(in_1));
  Register_File_1 register_file_1_1 (
    .Load(regWrite), .in_2(register_4_q), .Clk(Clock), .wr(Destination_Register), .rd1(multiplexer_4_out),
    .rd2(multiplexer_6_out), .outData1(Source_1), .outData2(Source_2));
  Stack_Pointer stack_pointer_1 (
    .Add_Sub_Select(or_5_out), .SP_address(out_4), .Enable(or_6_out), .Clock(Clock), .Clear(in_2));
  Comparator #(.width(10)) comparator_1 (.a(out_4), .b({10{1'b0}}), .eq(comparator_1_eq));  // open: gt, lt
  Register #(.width(1)) register_5 (.D(BG), .en(PCSelect), .Q(register_5_q), .clk(Clock), .clr(InstrRead));
  Register #(.width(1)) register_6 (.D(JumpDecider), .en(PCSelect), .Q(register_6_q), .clk(Clock), .clr(InstrRead));
  and and_2 (and_2_out, register_6_q, PCWriteSignal);
  Multiplexer #(.enable("false")) multiplexer_7 (.in0(and_2_out), .in1(and_3_out), .out(PCWrite), .sel(register_7_q));
  and and_3 (and_3_out, register_5_q, PCWriteSignal);
  Register #(.width(1)) register_7 (.D(Branch_Signal), .en(PCSelect), .Q(register_7_q), .clk(Clock), .clr(InstrRead));

  // Other names for the same wires on the sheet: Clear = in_2; DataFromMemory[19:0] = out_3; SP_Addr[9:0] = out_4

  // Notes on the sheet:
  //   contents of rom_1 (hex, n*v repeats v):
  //   70005 31001 42100 63100 4100 85100 c2000 b6000 f200b f1205 f1208 f0204 a0003 afffc afffd d3000 d5000
  //   e8000 e9000
endmodule

module Stack_Pointer (
  input  Add_Sub_Select,
  input  Enable,
  input  Clock,
  input  Clear,
  output [9:0] SP_address
);

  wire n20bit_comparator_1_1_eq;
  wire [19:0] add_sub_sum, multiplexer_1_out;
  wire [19:10] register_1_q;

  Adder___20_Bits add_sub (
    .Input_1(multiplexer_1_out), .sub_1_add_0(Add_Sub_Select), .Input_2(20'h1), .SUM(add_sub_sum));  // open: Overflow
  Register #(.width(20), .trigger("falling")) register_1 (
    .D(add_sub_sum), .en(Enable), .Q({register_1_q, SP_address}), .clk(Clock), .clr(Clear));
  Multiplexer #(.width(20), .enable("false")) multiplexer_1 (
    .in0({register_1_q, SP_address}), .in1(20'h100), .out(multiplexer_1_out), .sel(n20bit_comparator_1_1_eq));
  _20Bit_Comparator_1 u_20bit_comparator_1_1 (
    .in_1({20{1'b0}}), .in_2({register_1_q, SP_address}), .EQ(n20bit_comparator_1_1_eq));
endmodule
