// Logisim project ADDER.circ as structural Verilog: 5 circuits, main circuit Full Adder
// HA
module Half_Adder (
  input  A,
  input  B,
  output Sum,
  output Cout
);

  xor xor_1 (Sum, A, B);
  and and_1 (Cout, A, B);
endmodule

// FA
module Full_Adder (
  input  B,
  input  A,
  input  Cin,
  output Sum,
  output Cout
);

  wire and_1_out, and_2_out, xor_1_out;

  xor xor_1 (xor_1_out, B, A);
  and and_1 (and_1_out, B, A);
  xor xor_2 (Sum, xor_1_out, Cin);
  and and_2 (and_2_out, xor_1_out, Cin);
  or or_1 (Cout, and_2_out, and_1_out);
endmodule

module Adder__18_Bits (
  input  [17:0] Input_1,
  input  [17:0] Input_2,
  output Overflow,
  output [17:0] SUM
);

  wire _0_cout, _1_cout, _2_cout, _3_cout, _4_cout, _5_cout, _6_cout, _7_cout, _8_cout, _9_cout, _10_cout,
       _11_cout, _12_cout, _13_cout, _14_cout, _15_cout, _16_cout, _17_cout;

  Overflow_Detector overflow_detector_1 (
    .Input_1(Input_1[17]), .Input_2(Input_2[17]), .Sum_s_MSB(SUM[17]), .out_4(Overflow));
  Half_Adder _0 (.A(Input_1[0]), .B(Input_2[0]), .Sum(SUM[0]), .Cout(_0_cout));
  Full_Adder _1 (.B(Input_2[1]), .A(Input_1[1]), .Cin(_0_cout), .Sum(SUM[1]), .Cout(_1_cout));
  Full_Adder _2 (.B(Input_2[2]), .A(Input_1[2]), .Cin(_1_cout), .Sum(SUM[2]), .Cout(_2_cout));
  Full_Adder _3 (.B(Input_2[3]), .A(Input_1[3]), .Cin(_2_cout), .Sum(SUM[3]), .Cout(_3_cout));
  Full_Adder _4 (.B(Input_2[4]), .A(Input_1[4]), .Cin(_3_cout), .Sum(SUM[4]), .Cout(_4_cout));
  Full_Adder _5 (.B(Input_2[5]), .A(Input_1[5]), .Cin(_4_cout), .Sum(SUM[5]), .Cout(_5_cout));
  Full_Adder _6 (.B(Input_2[6]), .A(Input_1[6]), .Cin(_5_cout), .Sum(SUM[6]), .Cout(_6_cout));
  Full_Adder _7 (.B(Input_2[7]), .A(Input_1[7]), .Cin(_6_cout), .Sum(SUM[7]), .Cout(_7_cout));
  Full_Adder _8 (.B(Input_2[8]), .A(Input_1[8]), .Cin(_7_cout), .Sum(SUM[8]), .Cout(_8_cout));
  Full_Adder _9 (.B(Input_2[9]), .A(Input_1[9]), .Cin(_8_cout), .Sum(SUM[9]), .Cout(_9_cout));
  Full_Adder _10 (.B(Input_2[10]), .A(Input_1[10]), .Cin(_9_cout), .Sum(SUM[10]), .Cout(_10_cout));
  Full_Adder _11 (.B(Input_2[11]), .A(Input_1[11]), .Cin(_10_cout), .Sum(SUM[11]), .Cout(_11_cout));
  Full_Adder _12 (.B(Input_2[12]), .A(Input_1[12]), .Cin(_11_cout), .Sum(SUM[12]), .Cout(_12_cout));
  Full_Adder _13 (.B(Input_2[13]), .A(Input_1[13]), .Cin(_12_cout), .Sum(SUM[13]), .Cout(_13_cout));
  Full_Adder _14 (.B(Input_2[14]), .A(Input_1[14]), .Cin(_13_cout), .Sum(SUM[14]), .Cout(_14_cout));
  Full_Adder _15 (.B(Input_2[15]), .A(Input_1[15]), .Cin(_14_cout), .Sum(SUM[15]), .Cout(_15_cout));
  Full_Adder _16 (.B(Input_2[16]), .A(Input_1[16]), .Cin(_15_cout), .Sum(SUM[16]), .Cout(_16_cout));
  Full_Adder _17 (.B(Input_2[17]), .A(Input_1[17]), .Cin(_16_cout), .Sum(SUM[17]), .Cout(_17_cout));
endmodule

module Overflow_Detector (
  input  Input_1,
  input  Input_2,
  input  Sum_s_MSB,
  output out_4
);

  wire and_1_out, and_2_out, not_1_out, not_2_out, not_3_out;

  not not_1 (not_1_out, Input_1);
  not not_2 (not_2_out, Input_2);
  not not_3 (not_3_out, Sum_s_MSB);
  and and_1 (and_1_out, not_1_out, not_2_out, Sum_s_MSB);
  and and_2 (and_2_out, not_3_out, Input_2, Input_1);
  or or_1 (out_4, and_1_out, and_2_out);
endmodule

module Adder___20_Bits (
  input  [19:0] Input_1,
  input  sub_1_add_0,
  input  [19:0] Input_2,
  output Overflow,
  output [19:0] SUM
);

  wire _1_cout, _2_cout, _3_cout, _4_cout, _5_cout, _6_cout, _7_cout, _8_cout, _9_cout, _10_cout, _11_cout,
       _12_cout, _13_cout, _14_cout, _15_cout, _16_cout, _17_cout, full_adder_1_cout, full_adder_2_cout,
       full_adder_3_cout;
  wire [19:0] multiplexer_1_out, not_1_out;

  Multiplexer #(.width(20), .enable("false")) multiplexer_1 (
    .in0(Input_2), .in1(not_1_out), .out(multiplexer_1_out), .sel(sub_1_add_0));
  assign not_1_out = ~Input_2;  // NOT_Gate not_1, 20 bits wide
  Overflow_Detector overflow_detector_1 (
    .Input_1(Input_1[19]), .Input_2(multiplexer_1_out[19]), .Sum_s_MSB(SUM[19]), .out_4(Overflow));
  Full_Adder full_adder_1 (
    .B(multiplexer_1_out[0]), .A(Input_1[0]), .Cin(sub_1_add_0), .Sum(SUM[0]), .Cout(full_adder_1_cout));
  Full_Adder _1 (.B(multiplexer_1_out[1]), .A(Input_1[1]), .Cin(full_adder_1_cout), .Sum(SUM[1]), .Cout(_1_cout));
  Full_Adder _2 (.B(multiplexer_1_out[2]), .A(Input_1[2]), .Cin(_1_cout), .Sum(SUM[2]), .Cout(_2_cout));
  Full_Adder _3 (.B(multiplexer_1_out[3]), .A(Input_1[3]), .Cin(_2_cout), .Sum(SUM[3]), .Cout(_3_cout));
  Full_Adder _4 (.B(multiplexer_1_out[4]), .A(Input_1[4]), .Cin(_3_cout), .Sum(SUM[4]), .Cout(_4_cout));
  Full_Adder _5 (.B(multiplexer_1_out[5]), .A(Input_1[5]), .Cin(_4_cout), .Sum(SUM[5]), .Cout(_5_cout));
  Full_Adder _6 (.B(multiplexer_1_out[6]), .A(Input_1[6]), .Cin(_5_cout), .Sum(SUM[6]), .Cout(_6_cout));
  Full_Adder _7 (.B(multiplexer_1_out[7]), .A(Input_1[7]), .Cin(_6_cout), .Sum(SUM[7]), .Cout(_7_cout));
  Full_Adder _8 (.B(multiplexer_1_out[8]), .A(Input_1[8]), .Cin(_7_cout), .Sum(SUM[8]), .Cout(_8_cout));
  Full_Adder _9 (.B(multiplexer_1_out[9]), .A(Input_1[9]), .Cin(_8_cout), .Sum(SUM[9]), .Cout(_9_cout));
  Full_Adder _10 (.B(multiplexer_1_out[10]), .A(Input_1[10]), .Cin(_9_cout), .Sum(SUM[10]), .Cout(_10_cout));
  Full_Adder _11 (.B(multiplexer_1_out[11]), .A(Input_1[11]), .Cin(_10_cout), .Sum(SUM[11]), .Cout(_11_cout));
  Full_Adder _12 (.B(multiplexer_1_out[12]), .A(Input_1[12]), .Cin(_11_cout), .Sum(SUM[12]), .Cout(_12_cout));
  Full_Adder _13 (.B(multiplexer_1_out[13]), .A(Input_1[13]), .Cin(_12_cout), .Sum(SUM[13]), .Cout(_13_cout));
  Full_Adder _14 (.B(multiplexer_1_out[14]), .A(Input_1[14]), .Cin(_13_cout), .Sum(SUM[14]), .Cout(_14_cout));
  Full_Adder _15 (.B(multiplexer_1_out[15]), .A(Input_1[15]), .Cin(_14_cout), .Sum(SUM[15]), .Cout(_15_cout));
  Full_Adder _16 (.B(multiplexer_1_out[16]), .A(Input_1[16]), .Cin(_15_cout), .Sum(SUM[16]), .Cout(_16_cout));
  Full_Adder _17 (.B(multiplexer_1_out[17]), .A(Input_1[17]), .Cin(_16_cout), .Sum(SUM[17]), .Cout(_17_cout));
  Full_Adder full_adder_2 (
    .B(multiplexer_1_out[18]), .A(Input_1[18]), .Cin(_17_cout), .Sum(SUM[18]), .Cout(full_adder_2_cout));
  Full_Adder full_adder_3 (
    .B(multiplexer_1_out[19]), .A(Input_1[19]), .Cin(full_adder_2_cout), .Sum(SUM[19]),
    .Cout(full_adder_3_cout));
endmodule
