// Logisim project COMPARATORS.circ as structural Verilog
// HC
module Half_Comparator (
  input  A,
  input  B,
  output GT,
  output EQ,
  output LT
);

  wire not_1_out, not_2_out;

  not not_1 (not_1_out, B);
  not not_2 (not_2_out, A);
  and and_1 (LT, not_2_out, B);
  and and_2 (GT, A, not_1_out);
  xnor xnor_1 (EQ, A, B);
endmodule

// FC
module Full_Comparator (
  input  A,
  input  B,
  input  GT_IN,
  input  EQ_IN,
  input  LT_IN,
  output GT,
  output EQ,
  output LT
);

  wire and_1_out, and_2_out, not_1_out, not_2_out, xnor_1_out;

  not not_1 (not_1_out, B);
  and and_1 (and_1_out, not_1_out, A, EQ_IN);
  xnor xnor_1 (xnor_1_out, B, A);
  not not_2 (not_2_out, A);
  and and_2 (and_2_out, B, not_2_out, EQ_IN);
  or or_1 (GT, and_1_out, GT_IN);
  and and_3 (EQ, xnor_1_out, EQ_IN);
  or or_2 (LT, and_2_out, LT_IN);
endmodule

module _18BIT_COMPARATOR (
  input  [17:0] in_1,
  input  [17:0] in_2,
  output EQ,
  output GT,
  output LT
);

  wire full_comparator_1_eq, full_comparator_1_gt, full_comparator_1_lt, full_comparator_2_eq,
       full_comparator_2_gt, full_comparator_2_lt, full_comparator_3_eq, full_comparator_3_gt,
       full_comparator_3_lt, full_comparator_4_eq, full_comparator_4_gt, full_comparator_4_lt,
       full_comparator_5_eq, full_comparator_5_gt, full_comparator_5_lt, full_comparator_6_eq,
       full_comparator_6_gt, full_comparator_6_lt, full_comparator_7_eq, full_comparator_7_gt,
       full_comparator_7_lt, full_comparator_8_eq, full_comparator_8_gt, full_comparator_8_lt,
       full_comparator_9_eq, full_comparator_9_gt, full_comparator_9_lt, full_comparator_10_eq,
       full_comparator_10_gt, full_comparator_10_lt, full_comparator_11_eq, full_comparator_11_gt,
       full_comparator_11_lt, full_comparator_12_eq, full_comparator_12_gt, full_comparator_12_lt,
       full_comparator_13_eq, full_comparator_13_gt, full_comparator_13_lt, full_comparator_14_eq,
       full_comparator_14_gt, full_comparator_14_lt, full_comparator_15_eq, full_comparator_15_gt,
       full_comparator_15_lt, full_comparator_16_eq, full_comparator_16_gt, full_comparator_16_lt,
       half_comparator_1_eq, half_comparator_1_gt, half_comparator_1_lt;

  Half_Comparator half_comparator_1 (
    .A(in_1[17]), .GT(half_comparator_1_gt), .EQ(half_comparator_1_eq), .LT(half_comparator_1_lt),
    .B(in_2[17]));
  Full_Comparator full_comparator_1 (
    .A(in_1[16]), .GT_IN(half_comparator_1_gt), .EQ_IN(half_comparator_1_eq), .LT_IN(half_comparator_1_lt),
    .GT(full_comparator_1_gt), .EQ(full_comparator_1_eq), .LT(full_comparator_1_lt), .B(in_2[16]));
  Full_Comparator full_comparator_2 (
    .A(in_1[15]), .GT_IN(full_comparator_1_gt), .EQ_IN(full_comparator_1_eq), .LT_IN(full_comparator_1_lt),
    .GT(full_comparator_2_gt), .EQ(full_comparator_2_eq), .LT(full_comparator_2_lt), .B(in_2[15]));
  Full_Comparator full_comparator_3 (
    .A(in_1[14]), .GT_IN(full_comparator_2_gt), .EQ_IN(full_comparator_2_eq), .LT_IN(full_comparator_2_lt),
    .GT(full_comparator_3_gt), .EQ(full_comparator_3_eq), .LT(full_comparator_3_lt), .B(in_2[14]));
  Full_Comparator full_comparator_4 (
    .A(in_1[13]), .GT_IN(full_comparator_3_gt), .EQ_IN(full_comparator_3_eq), .LT_IN(full_comparator_3_lt),
    .GT(full_comparator_4_gt), .EQ(full_comparator_4_eq), .LT(full_comparator_4_lt), .B(in_2[13]));
  Full_Comparator full_comparator_5 (
    .A(in_1[12]), .GT_IN(full_comparator_4_gt), .EQ_IN(full_comparator_4_eq), .LT_IN(full_comparator_4_lt),
    .GT(full_comparator_5_gt), .EQ(full_comparator_5_eq), .LT(full_comparator_5_lt), .B(in_2[12]));
  Full_Comparator full_comparator_6 (
    .A(in_1[11]), .GT_IN(full_comparator_5_gt), .EQ_IN(full_comparator_5_eq), .LT_IN(full_comparator_5_lt),
    .GT(full_comparator_6_gt), .EQ(full_comparator_6_eq), .LT(full_comparator_6_lt), .B(in_2[11]));
  Full_Comparator full_comparator_7 (
    .A(in_1[10]), .GT_IN(full_comparator_6_gt), .EQ_IN(full_comparator_6_eq), .LT_IN(full_comparator_6_lt),
    .GT(full_comparator_7_gt), .EQ(full_comparator_7_eq), .LT(full_comparator_7_lt), .B(in_2[10]));
  Full_Comparator full_comparator_8 (
    .A(in_1[9]), .GT_IN(full_comparator_7_gt), .EQ_IN(full_comparator_7_eq), .LT_IN(full_comparator_7_lt),
    .GT(full_comparator_8_gt), .EQ(full_comparator_8_eq), .LT(full_comparator_8_lt), .B(in_2[9]));
  Full_Comparator full_comparator_9 (
    .A(in_1[8]), .GT_IN(full_comparator_8_gt), .EQ_IN(full_comparator_8_eq), .LT_IN(full_comparator_8_lt),
    .GT(full_comparator_9_gt), .EQ(full_comparator_9_eq), .LT(full_comparator_9_lt), .B(in_2[8]));
  Full_Comparator full_comparator_10 (
    .A(in_1[7]), .GT_IN(full_comparator_9_gt), .EQ_IN(full_comparator_9_eq), .LT_IN(full_comparator_9_lt),
    .GT(full_comparator_10_gt), .EQ(full_comparator_10_eq), .LT(full_comparator_10_lt), .B(in_2[7]));
  Full_Comparator full_comparator_11 (
    .A(in_1[6]), .GT_IN(full_comparator_10_gt), .EQ_IN(full_comparator_10_eq), .LT_IN(full_comparator_10_lt),
    .GT(full_comparator_11_gt), .EQ(full_comparator_11_eq), .LT(full_comparator_11_lt), .B(in_2[6]));
  Full_Comparator full_comparator_12 (
    .A(in_1[5]), .GT_IN(full_comparator_11_gt), .EQ_IN(full_comparator_11_eq), .LT_IN(full_comparator_11_lt),
    .GT(full_comparator_12_gt), .EQ(full_comparator_12_eq), .LT(full_comparator_12_lt), .B(in_2[5]));
  Full_Comparator full_comparator_13 (
    .A(in_1[4]), .GT_IN(full_comparator_12_gt), .EQ_IN(full_comparator_12_eq), .LT_IN(full_comparator_12_lt),
    .GT(full_comparator_13_gt), .EQ(full_comparator_13_eq), .LT(full_comparator_13_lt), .B(in_2[4]));
  Full_Comparator full_comparator_14 (
    .A(in_1[3]), .GT_IN(full_comparator_13_gt), .EQ_IN(full_comparator_13_eq), .LT_IN(full_comparator_13_lt),
    .GT(full_comparator_14_gt), .EQ(full_comparator_14_eq), .LT(full_comparator_14_lt), .B(in_2[3]));
  Full_Comparator full_comparator_15 (
    .A(in_1[2]), .GT_IN(full_comparator_14_gt), .EQ_IN(full_comparator_14_eq), .LT_IN(full_comparator_14_lt),
    .GT(full_comparator_15_gt), .EQ(full_comparator_15_eq), .LT(full_comparator_15_lt), .B(in_2[2]));
  Full_Comparator full_comparator_16 (
    .A(in_1[1]), .GT_IN(full_comparator_15_gt), .EQ_IN(full_comparator_15_eq), .LT_IN(full_comparator_15_lt),
    .GT(full_comparator_16_gt), .EQ(full_comparator_16_eq), .LT(full_comparator_16_lt), .B(in_2[1]));
  Full_Comparator full_comparator_17 (
    .A(in_1[0]), .GT_IN(full_comparator_16_gt), .EQ_IN(full_comparator_16_eq), .LT_IN(full_comparator_16_lt),
    .GT(GT), .EQ(EQ), .LT(LT), .B(in_2[0]));
endmodule

module Half_Comparator_1 (
  input  A,
  input  B,
  output EQ
);

  xnor xnor_1 (EQ, A, B);
endmodule

module Full_Comparator_1 (
  input  A,
  input  B,
  input  EQ_IN,
  output EQ
);

  wire xnor_1_out;

  xnor xnor_1 (xnor_1_out, B, A);
  and and_1 (EQ, xnor_1_out, EQ_IN);
endmodule

module _20Bit_Comparator_1 (
  input  [19:0] in_1,
  input  [19:0] in_2,
  output EQ
);

  wire full_comparator_1_1_eq, full_comparator_1_2_eq, full_comparator_1_3_eq, full_comparator_1_4_eq,
       full_comparator_1_5_eq, full_comparator_1_6_eq, full_comparator_1_7_eq, full_comparator_1_8_eq,
       full_comparator_1_9_eq, full_comparator_1_10_eq, full_comparator_1_11_eq, full_comparator_1_12_eq,
       full_comparator_1_13_eq, full_comparator_1_14_eq, full_comparator_1_15_eq, full_comparator_1_16_eq,
       full_comparator_1_17_eq, full_comparator_1_18_eq, half_comparator_1_1_eq;

  Half_Comparator_1 half_comparator_1_1 (.A(in_1[19]), .EQ(half_comparator_1_1_eq), .B(in_2[19]));
  Full_Comparator_1 full_comparator_1_1 (
    .A(in_1[18]), .EQ_IN(half_comparator_1_1_eq), .EQ(full_comparator_1_1_eq), .B(in_2[18]));
  Full_Comparator_1 full_comparator_1_2 (
    .A(in_1[17]), .EQ_IN(full_comparator_1_1_eq), .EQ(full_comparator_1_2_eq), .B(in_2[17]));
  Full_Comparator_1 full_comparator_1_3 (
    .A(in_1[16]), .EQ_IN(full_comparator_1_2_eq), .EQ(full_comparator_1_3_eq), .B(in_2[16]));
  Full_Comparator_1 full_comparator_1_4 (
    .A(in_1[15]), .EQ_IN(full_comparator_1_3_eq), .EQ(full_comparator_1_4_eq), .B(in_2[15]));
  Full_Comparator_1 full_comparator_1_5 (
    .A(in_1[14]), .EQ_IN(full_comparator_1_4_eq), .EQ(full_comparator_1_5_eq), .B(in_2[14]));
  Full_Comparator_1 full_comparator_1_6 (
    .A(in_1[13]), .EQ_IN(full_comparator_1_5_eq), .EQ(full_comparator_1_6_eq), .B(in_2[13]));
  Full_Comparator_1 full_comparator_1_7 (
    .A(in_1[12]), .EQ_IN(full_comparator_1_6_eq), .EQ(full_comparator_1_7_eq), .B(in_2[12]));
  Full_Comparator_1 full_comparator_1_8 (
    .A(in_1[11]), .EQ_IN(full_comparator_1_7_eq), .EQ(full_comparator_1_8_eq), .B(in_2[11]));
  Full_Comparator_1 full_comparator_1_9 (
    .A(in_1[10]), .EQ_IN(full_comparator_1_8_eq), .EQ(full_comparator_1_9_eq), .B(in_2[10]));
  Full_Comparator_1 full_comparator_1_10 (
    .A(in_1[9]), .EQ_IN(full_comparator_1_9_eq), .EQ(full_comparator_1_10_eq), .B(in_2[9]));
  Full_Comparator_1 full_comparator_1_11 (
    .A(in_1[8]), .EQ_IN(full_comparator_1_10_eq), .EQ(full_comparator_1_11_eq), .B(in_2[8]));
  Full_Comparator_1 full_comparator_1_12 (
    .A(in_1[7]), .EQ_IN(full_comparator_1_11_eq), .EQ(full_comparator_1_12_eq), .B(in_2[7]));
  Full_Comparator_1 full_comparator_1_13 (
    .A(in_1[6]), .EQ_IN(full_comparator_1_12_eq), .EQ(full_comparator_1_13_eq), .B(in_2[6]));
  Full_Comparator_1 full_comparator_1_14 (
    .A(in_1[5]), .EQ_IN(full_comparator_1_13_eq), .EQ(full_comparator_1_14_eq), .B(in_2[5]));
  Full_Comparator_1 full_comparator_1_15 (
    .A(in_1[4]), .EQ_IN(full_comparator_1_14_eq), .EQ(full_comparator_1_15_eq), .B(in_2[4]));
  Full_Comparator_1 full_comparator_1_16 (
    .A(in_1[3]), .EQ_IN(full_comparator_1_15_eq), .EQ(full_comparator_1_16_eq), .B(in_2[3]));
  Full_Comparator_1 full_comparator_1_17 (
    .A(in_1[2]), .EQ_IN(full_comparator_1_16_eq), .EQ(full_comparator_1_17_eq), .B(in_2[2]));
  Full_Comparator_1 full_comparator_1_18 (
    .A(in_1[1]), .EQ_IN(full_comparator_1_17_eq), .EQ(full_comparator_1_18_eq), .B(in_2[1]));
  Full_Comparator_1 full_comparator_1_19 (.A(in_1[0]), .EQ_IN(full_comparator_1_18_eq), .EQ(EQ), .B(in_2[0]));
endmodule
