// Logisim project MAIN.circ as structural Verilog: 14 circuits, main circuit CPU
module Register_File (
  input  Load,
  input  [17:0] in_2,
  input  Clk,
  input  [3:0] wr,
  input  [3:0] rd1,
  input  [3:0] rd2,
  output [17:0] outData1,
  output [17:0] outData2
);

  wire and_1_out, and_2_out, and_3_out, and_4_out, and_5_out, and_6_out, and_7_out, and_8_out, and_9_out,
       and_10_out, and_11_out, and_12_out, and_13_out, and_14_out, and_15_out, and_16_out, decoder_1_out0,
       decoder_1_out1, decoder_1_out2, decoder_1_out3, decoder_1_out4, decoder_1_out5, decoder_1_out6,
       decoder_1_out7, decoder_1_out8, decoder_1_out9, decoder_1_out10, decoder_1_out11, decoder_1_out12,
       decoder_1_out13, decoder_1_out14, decoder_1_out15, decoder_2_out0, decoder_2_out1, decoder_2_out2,
       decoder_2_out3, decoder_2_out4, decoder_2_out5, decoder_2_out6, decoder_2_out7, decoder_2_out8,
       decoder_2_out9, decoder_2_out10, decoder_2_out11, decoder_2_out12, decoder_2_out13, decoder_2_out14,
       decoder_2_out15, decoder_3_out0, decoder_3_out1, decoder_3_out2, decoder_3_out3, decoder_3_out4,
       decoder_3_out5, decoder_3_out6, decoder_3_out7, decoder_3_out8, decoder_3_out9, decoder_3_out10,
       decoder_3_out11, decoder_3_out12, decoder_3_out13, decoder_3_out14, decoder_3_out15;
  wire [17:0] R0_q, R1_q, R2_q, R3_q, R4_q, R5_q, R6_q, R7_q, R8_q, R9_q, R10_q, R11_q, R12_q, R13_q, R14_q,
       R15_q;

  Decoder #(.select(4), .enable("false")) decoder_1 (
    .out0(decoder_1_out0), .out1(decoder_1_out1), .out2(decoder_1_out2), .out3(decoder_1_out3),
    .out4(decoder_1_out4), .out5(decoder_1_out5), .out6(decoder_1_out6), .out7(decoder_1_out7),
    .out8(decoder_1_out8), .out9(decoder_1_out9), .out10(decoder_1_out10), .out11(decoder_1_out11),
    .out12(decoder_1_out12), .out13(decoder_1_out13), .out14(decoder_1_out14), .out15(decoder_1_out15),
    .sel(wr));
  and and_1 (and_1_out, Load, decoder_1_out0);
  and and_2 (and_2_out, Load, decoder_1_out1);
  and and_3 (and_3_out, Load, decoder_1_out2);
  and and_4 (and_4_out, Load, decoder_1_out3);
  and and_5 (and_5_out, Load, decoder_1_out4);
  and and_6 (and_6_out, Load, decoder_1_out5);
  and and_7 (and_7_out, Load, decoder_1_out6);
  and and_8 (and_8_out, Load, decoder_1_out7);
  Register #(.width(18)) R0 (.D(in_2), .en(and_1_out), .Q(R0_q), .clk(Clk), .clr(1'b0));
  Register #(.width(18)) R1 (.D(in_2), .en(and_2_out), .Q(R1_q), .clk(Clk), .clr(1'b0));
  Register #(.width(18)) R2 (.D(in_2), .en(and_3_out), .Q(R2_q), .clk(Clk), .clr(1'b0));
  Register #(.width(18)) R3 (.D(in_2), .en(and_4_out), .Q(R3_q), .clk(Clk), .clr(1'b0));
  Register #(.width(18)) R4 (.D(in_2), .en(and_5_out), .Q(R4_q), .clk(Clk), .clr(1'b0));
  Register #(.width(18)) R5 (.D(in_2), .en(and_6_out), .Q(R5_q), .clk(Clk), .clr(1'b0));
  Register #(.width(18)) R6 (.D(in_2), .en(and_7_out), .Q(R6_q), .clk(Clk), .clr(1'b0));
  Register #(.width(18)) R7 (.D(in_2), .en(and_8_out), .Q(R7_q), .clk(Clk), .clr(1'b0));
  and and_9 (and_9_out, Load, decoder_1_out8);
  and and_10 (and_10_out, Load, decoder_1_out9);
  and and_11 (and_11_out, Load, decoder_1_out10);
  and and_12 (and_12_out, Load, decoder_1_out11);
  and and_13 (and_13_out, Load, decoder_1_out12);
  and and_14 (and_14_out, Load, decoder_1_out13);
  and and_15 (and_15_out, Load, decoder_1_out14);
  and and_16 (and_16_out, Load, decoder_1_out15);
  Decoder #(.select(4), .enable("false")) decoder_2 (
    .out0(decoder_2_out0), .out1(decoder_2_out1), .out2(decoder_2_out2), .out3(decoder_2_out3),
    .out4(decoder_2_out4), .out5(decoder_2_out5), .out6(decoder_2_out6), .out7(decoder_2_out7),
    .out8(decoder_2_out8), .out9(decoder_2_out9), .out10(decoder_2_out10), .out11(decoder_2_out11),
    .out12(decoder_2_out12), .out13(decoder_2_out13), .out14(decoder_2_out14), .out15(decoder_2_out15),
    .sel(rd1));
  Decoder #(.select(4), .enable("false")) decoder_3 (
    .out0(decoder_3_out0), .out1(decoder_3_out1), .out2(decoder_3_out2), .out3(decoder_3_out3),
    .out4(decoder_3_out4), .out5(decoder_3_out5), .out6(decoder_3_out6), .out7(decoder_3_out7),
    .out8(decoder_3_out8), .out9(decoder_3_out9), .out10(decoder_3_out10), .out11(decoder_3_out11),
    .out12(decoder_3_out12), .out13(decoder_3_out13), .out14(decoder_3_out14), .out15(decoder_3_out15),
    .sel(rd2));
  Register #(.width(18)) R8 (.D(in_2), .en(and_9_out), .Q(R8_q), .clk(Clk), .clr(1'b0));
  Register #(.width(18)) R9 (.D(in_2), .en(and_10_out), .Q(R9_q), .clk(Clk), .clr(1'b0));
  Register #(.width(18)) R10 (.D(in_2), .en(and_11_out), .Q(R10_q), .clk(Clk), .clr(1'b0));
  Register #(.width(18)) R11 (.D(in_2), .en(and_12_out), .Q(R11_q), .clk(Clk), .clr(1'b0));
  Register #(.width(18)) R12 (.D(in_2), .en(and_13_out), .Q(R12_q), .clk(Clk), .clr(1'b0));
  Register #(.width(18)) R13 (.D(in_2), .en(and_14_out), .Q(R13_q), .clk(Clk), .clr(1'b0));
  Register #(.width(18)) R14 (.D(in_2), .en(and_15_out), .Q(R14_q), .clk(Clk), .clr(1'b0));
  Register #(.width(18)) R15 (.D(in_2), .en(and_16_out), .Q(R15_q), .clk(Clk), .clr(1'b0));
  assign outData1 = decoder_2_out0 ? R0_q : 18'bz;  // Controlled_Buffer controlled_buffer_1
  assign outData2 = decoder_3_out0 ? R0_q : 18'bz;  // Controlled_Buffer controlled_buffer_2
  assign outData1 = decoder_2_out1 ? R1_q : 18'bz;  // Controlled_Buffer controlled_buffer_3
  assign outData2 = decoder_3_out1 ? R1_q : 18'bz;  // Controlled_Buffer controlled_buffer_4
  assign outData1 = decoder_2_out2 ? R2_q : 18'bz;  // Controlled_Buffer controlled_buffer_5
  assign outData2 = decoder_3_out2 ? R2_q : 18'bz;  // Controlled_Buffer controlled_buffer_6
  assign outData1 = decoder_2_out3 ? R3_q : 18'bz;  // Controlled_Buffer controlled_buffer_7
  assign outData2 = decoder_3_out3 ? R3_q : 18'bz;  // Controlled_Buffer controlled_buffer_8
  assign outData1 = decoder_2_out4 ? R4_q : 18'bz;  // Controlled_Buffer controlled_buffer_9
  assign outData2 = decoder_3_out4 ? R4_q : 18'bz;  // Controlled_Buffer controlled_buffer_10
  assign outData1 = decoder_2_out5 ? R5_q : 18'bz;  // Controlled_Buffer controlled_buffer_11
  assign outData2 = decoder_3_out5 ? R5_q : 18'bz;  // Controlled_Buffer controlled_buffer_12
  assign outData1 = decoder_2_out6 ? R6_q : 18'bz;  // Controlled_Buffer controlled_buffer_13
  assign outData2 = decoder_3_out6 ? R6_q : 18'bz;  // Controlled_Buffer controlled_buffer_14
  assign outData1 = decoder_2_out7 ? R7_q : 18'bz;  // Controlled_Buffer controlled_buffer_15
  assign outData2 = decoder_3_out7 ? R7_q : 18'bz;  // Controlled_Buffer controlled_buffer_16
  assign outData1 = decoder_2_out8 ? R8_q : 18'bz;  // Controlled_Buffer controlled_buffer_17
  assign outData2 = decoder_3_out8 ? R8_q : 18'bz;  // Controlled_Buffer controlled_buffer_18
  assign outData1 = decoder_2_out9 ? R9_q : 18'bz;  // Controlled_Buffer controlled_buffer_19
  assign outData2 = decoder_3_out9 ? R9_q : 18'bz;  // Controlled_Buffer controlled_buffer_20
  assign outData1 = decoder_2_out10 ? R10_q : 18'bz;  // Controlled_Buffer controlled_buffer_21
  assign outData2 = decoder_3_out10 ? R10_q : 18'bz;  // Controlled_Buffer controlled_buffer_22
  assign outData1 = decoder_2_out11 ? R11_q : 18'bz;  // Controlled_Buffer controlled_buffer_23
  assign outData2 = decoder_3_out11 ? R11_q : 18'bz;  // Controlled_Buffer controlled_buffer_24
  assign outData1 = decoder_2_out12 ? R12_q : 18'bz;  // Controlled_Buffer controlled_buffer_25
  assign outData2 = decoder_3_out12 ? R12_q : 18'bz;  // Controlled_Buffer controlled_buffer_26
  assign outData1 = decoder_2_out13 ? R13_q : 18'bz;  // Controlled_Buffer controlled_buffer_27
  assign outData2 = decoder_3_out13 ? R13_q : 18'bz;  // Controlled_Buffer controlled_buffer_28
  assign outData1 = decoder_2_out14 ? R14_q : 18'bz;  // Controlled_Buffer controlled_buffer_29
  assign outData2 = decoder_3_out14 ? R14_q : 18'bz;  // Controlled_Buffer controlled_buffer_30
  assign outData1 = decoder_2_out15 ? R15_q : 18'bz;  // Controlled_Buffer controlled_buffer_31
  assign outData2 = decoder_3_out15 ? R15_q : 18'bz;  // Controlled_Buffer controlled_buffer_32
endmodule

module PC_File (
  input  [17:0] JUMP_ADDRESS,
  input  Clear,
  input  Enable,
  input  Clock,
  input  ADDRSelect,
  output [17:0] PC_address
);

  wire [17:0] adder_18_bits_1_sum, multiplexer_1_out, multiplexer_2_out;

  Multiplexer #(.width(18)) multiplexer_1 (
    .in0(18'h1), .in1(JUMP_ADDRESS), .out(multiplexer_1_out), .sel(ADDRSelect));  // open: en
  Adder__18_Bits adder_18_bits_1 (
    .Input_1(multiplexer_1_out), .Input_2(multiplexer_2_out), .SUM(adder_18_bits_1_sum));  // open: Overflow
  Multiplexer #(.width(18)) multiplexer_2 (
    .in0(PC_address), .in1({18{1'b0}}), .out(multiplexer_2_out), .sel(ADDRSelect));  // open: en
  Register #(.width(18), .trigger("falling")) register_1 (
    .D(adder_18_bits_1_sum), .en(Enable), .Q(PC_address), .clk(Clock), .clr(Clear));
endmodule

// 1
module CPU (
  input  in_1,
  input  in_2,
  input  in_3,
  output [17:0] out_4
);

  wire ALU_Signal, and_1_out, and_2_out, and_3_out, BG, Branch_Signal, Clock, Immediate_Signal, InstrRead,
       JumpDecider, Memory_Read, Memory_Write, or_1_out, or_2_out, or_4_out, PCRead, PCSelect, PCWrite,
       PCWriteSignal, register_1_q, register_4_q, register_5_q, register_6_q, regWrite;
  wire [1:0] ALU_Bits;
  wire [2:0] NZP;
  wire [3:0] Destination_Register, multiplexer_4_out, multiplexer_5_out, Source_Register, SR1, SR2;
  wire [9:0] Address10;
  wire [17:0] adder_18_bits_1_sum, Address3, AluResult, ExtendJump, Immediate, Instr, multiplexer_1_out,
       multiplexer_2_out, multiplexer_6_out, PC_Value, register_2_q, register_3_q, rom_1_data, Source_1,
       Source_2;

  Clock clock_1 (.out(Clock));
  Multiplexer #(.width(18)) multiplexer_1 (
    .in0(ExtendJump), .in1(Address3), .out(multiplexer_1_out), .sel(Branch_Signal));  // open: en
  Control_Unit control_unit_1 (
    .Memory_Write(Memory_Write), .JumpDecider(JumpDecider), .Memory_Read(Memory_Read), .Reg_Write(regWrite),
    .PCRead(PCRead), .InstrRead(InstrRead), .in_3(in_1), .in_2(Clock), .Instruction(Instr),
    .ALU_Signal(ALU_Signal), .Immediate_Signal(Immediate_Signal), .Branch_Signal(Branch_Signal),
    .PCWrite(PCWriteSignal));
  SignExtendValue signextendvalue_1 (.Input(Instr), .Output(ExtendJump));
  Adder__18_Bits adder_18_bits_1 (
    .Input_1(multiplexer_1_out), .Input_2(PC_Value), .SUM(adder_18_bits_1_sum));  // open: Overflow
  Register #(.width(1)) register_1 (.D(PCWrite), .en(PCWrite), .Q(register_1_q), .clk(Clock), .clr(InstrRead));
  or or_1 (or_1_out, Memory_Read, Immediate_Signal, ALU_Signal);
  Register #(.width(18)) register_2 (
    .D(adder_18_bits_1_sum), .en(PCSelect), .Q(register_2_q), .clk(Clock), .clr(InstrRead));
  Multiplexer #(.width(18)) multiplexer_2 (
    .in0(out_4), .in1(AluResult), .out(multiplexer_2_out), .sel(or_2_out));  // open: en
  or or_2 (or_2_out, ALU_Signal, Immediate_Signal);
  Register #(.width(18)) register_3 (.D(multiplexer_2_out), .en(or_1_out), .Q(register_3_q), .clk(Clock), .clr(in_1));
  or or_3 (PCSelect, JumpDecider, and_1_out);
  and and_1 (and_1_out, BG, Branch_Signal);
  Register #(.width(1)) register_4 (.D(BG), .en(PCSelect), .Q(register_4_q), .clk(Clock), .clr(InstrRead));
  PC_File pc_file_1 (
    .JUMP_ADDRESS(register_2_q), .ADDRSelect(register_1_q), .PC_address(PC_Value), .Enable(PCRead),
    .Clock(Clock), .Clear(in_1));
  Register #(.width(1)) register_5 (.D(JumpDecider), .en(PCSelect), .Q(register_5_q), .clk(Clock), .clr(InstrRead));
  or or_4 (or_4_out, ALU_Signal, Immediate_Signal);
  and and_2 (and_2_out, register_4_q, PCWriteSignal);
  and and_3 (and_3_out, register_5_q, PCWriteSignal);
  Multiplexer multiplexer_3 (.in0(and_3_out), .in1(and_2_out), .out(PCWrite), .sel(register_6_q));  // open: en
  Register #(.width(1)) register_6 (.D(Branch_Signal), .en(PCSelect), .Q(register_6_q), .clk(Clock), .clr(InstrRead));
  Multiplexer #(.width(4)) multiplexer_4 (
    .in0(Source_Register), .in1(SR1), .out(multiplexer_4_out), .sel(or_4_out));  // open: en
  ROM #(.addrWidth(18), .dataWidth(18)) rom_1 (.addr(PC_Value), .data(rom_1_data), .sel(in_2));
  Multiplexer #(.width(4)) multiplexer_5 (
    .in0(SR2), .in1(SR1), .out(multiplexer_5_out), .sel(Branch_Signal));  // open: en
  Register #(.width(18)) register_7 (.D(rom_1_data), .en(InstrRead), .Q(Instr), .clk(Clock), .clr(in_1));
  Register_File register_file_1 (
    .Load(regWrite), .Clk(Clock), .wr(Destination_Register), .rd1(multiplexer_4_out),
    .rd2(multiplexer_5_out), .outData1(Source_1), .outData2(Source_2), .in_2(register_3_q));
  InstructionParser instructionparser_1 (
    .Instruction(Instr), .ALU_Bits(ALU_Bits), .Address3(Address3), .SR2(SR2), .NZP(NZP),
    .Destination_Register(Destination_Register), .Address10(Address10), .Source_Register(Source_Register),
    .SR1(SR1), .Imm(Immediate));
  RAM #(.addrWidth(10), .dataWidth(18), .bus("separate")) ram_1 (
    .addr(Address10), .din(Source_1), .data(out_4), .str(Memory_Write), .sel(1'b1), .clk(Clock),
    .ld(Memory_Read), .clr(in_3));
  Multiplexer #(.width(18)) multiplexer_6 (
    .in0(Immediate), .in1(Source_2), .out(multiplexer_6_out), .sel(ALU_Signal));  // open: en
  ALU__New alu_new_1 (.Input_1(Source_1), .Input_2(multiplexer_6_out), .ALU_Controller(ALU_Bits), .ALU_Out(AluResult));
  BranchSignal branchsignal_1 (.input1(Source_1), .input2(Source_2), .nzp(NZP), .out_4(BG));

  // Other names for the same wires on the sheet: Clear = in_1; DataFromMemory[17:0] = out_4

  // Notes on the sheet:
  //   contents of rom_1 (hex, n*v repeats v):
  //   4000 4440 4880 4cc0 5100 20000 20401 c8bf 8cc4 18448 c441 340d3 28004 d101 8004 2bffc 25002 24003
  //   28000
endmodule

// Control Unit
module Control_Unit (
  input  [17:0] Instruction,
  input  in_2,
  input  in_3,
  output ALU_Signal,
  output Immediate_Signal,
  output Memory_Write,
  output JumpDecider,
  output Memory_Read,
  output Reg_Write,
  output Branch_Signal,
  output PCWrite,
  output PCRead,
  output InstrRead
);

  wire decoder_2_out0, decoder_2_out1, decoder_2_out2, decoder_2_out3, decoder_2_out4, decoder_2_out5,
       decoder_2_out6, decoder_2_out7, decoder_2_out8, decoder_2_out9, decoder_2_out10, decoder_2_out11,
       decoder_2_out12, decoder_2_out13, decoder_2_out14, decoder_2_out15, JumpState1, not_1_out, or_1_out,
       or_2_out, or_3_out, or_4_out, or_5_out, State3, State4;
  wire [1:0] counter_1_q;

  and and_1 (JumpState1, Memory_Write, State3);
  not not_1 (not_1_out, JumpState1);
  Counter #(.width(2), .max('h3)) counter_1 (
    .load(JumpState1), .D(2'b11), .count(not_1_out), .Q(counter_1_q), .clk(in_2), .clr(in_3));  // open: carry
  Decoder #(.select(2)) decoder_1 (
    .out0(InstrRead), .out1(State3), .out2(State4), .out3(PCRead), .sel(counter_1_q));  // open: en
  Decoder #(.select(4)) decoder_2 (
    .out0(decoder_2_out0), .out1(decoder_2_out1), .out2(decoder_2_out2), .out3(decoder_2_out3),
    .out4(decoder_2_out4), .out5(decoder_2_out5), .out6(decoder_2_out6), .out7(decoder_2_out7),
    .out8(decoder_2_out8), .out9(decoder_2_out9), .out10(decoder_2_out10), .out11(decoder_2_out11),
    .out12(decoder_2_out12), .out13(decoder_2_out13), .out14(decoder_2_out14), .out15(decoder_2_out15),
    .sel(Instruction[17:14]));  // open: en
  or or_1 (or_1_out, decoder_2_out15, decoder_2_out14, decoder_2_out13, decoder_2_out12, decoder_2_out11);
  and and_2 (Branch_Signal, State3, or_1_out);
  or or_2 (or_2_out, or_1_out, decoder_2_out10);
  and and_3 (Memory_Write, State3, decoder_2_out9);
  and and_4 (JumpDecider, State3, decoder_2_out10);
  and and_5 (Memory_Read, State3, decoder_2_out8);
  and and_6 (PCWrite, State4, or_2_out);
  or or_3 (or_3_out, decoder_2_out0, decoder_2_out2, decoder_2_out4, decoder_2_out6);
  or or_4 (or_4_out, decoder_2_out1, decoder_2_out3, decoder_2_out5, decoder_2_out7);
  and and_7 (ALU_Signal, or_3_out, State3);
  or or_5 (or_5_out, or_4_out, decoder_2_out6, decoder_2_out0, decoder_2_out2, decoder_2_out4, decoder_2_out8);
  and and_8 (Immediate_Signal, or_4_out, State3);
  and and_9 (Reg_Write, State4, or_5_out);

  // Other names for the same wires on the sheet: ResetControl = Memory_Write; State1 = PCRead; State2 = InstrRead
endmodule

module SignExtendValue (
  input  [17:0] Input,
  output [17:0] Output
);


  assign Output = {{5{Input[13]}}, Input[12:0]};
endmodule

module InstructionParser (
  input  [17:0] Instruction,
  output [17:0] Address3,
  output [3:0] SR2,
  output [2:0] NZP,
  output [1:0] ALU_Bits,
  output [3:0] Destination_Register,
  output [9:0] Address10,
  output [3:0] Source_Register,
  output [3:0] SR1,
  output [17:0] Imm
);

  assign Address3 = {{15{Instruction[5]}}, Instruction[5:3]};  // Bit_Extender bit_extender_1
  assign Imm = {{12{Instruction[5]}}, Instruction[5:0]};  // Bit_Extender bit_extender_2

  assign Address10 = Instruction[9:0];
  assign ALU_Bits = Instruction[16:15];
  assign Destination_Register = Instruction[13:10];
  assign NZP = Instruction[2:0];
  assign Source_Register = Instruction[13:10];
  assign SR1 = Instruction[9:6];
  assign SR2 = Instruction[5:2];

  // Other names for the same wires on the sheet: Opcode[3:0] = Instruction[17:14]
endmodule

module ALU__New (
  input  [17:0] Input_1,
  input  [17:0] Input_2,
  input  [1:0] ALU_Controller,
  output [17:0] ALU_Out
);

  wire [17:0] adder_18_bits_1_sum, and_1_out, or_1_out, xor_1_out;

  assign and_1_out = Input_1 & Input_2;  // AND_Gate and_1, 18 bits wide
  Adder__18_Bits adder_18_bits_1 (.Input_1(Input_1), .Input_2(Input_2), .SUM(adder_18_bits_1_sum));  // open: Overflow
  assign or_1_out = Input_1 | Input_2;  // OR_Gate or_1, 18 bits wide
  assign xor_1_out = Input_1 ^ Input_2;  // XOR_Gate xor_1, 18 bits wide
  Multiplexer #(.select(2), .width(18), .enable("false")) multiplexer_1 (
    .in0(and_1_out), .in1(adder_18_bits_1_sum), .in2(or_1_out), .in3(xor_1_out), .out(ALU_Out),
    .sel(ALU_Controller));
endmodule

module BranchSignal (
  input  [17:0] input1,
  input  [17:0] input2,
  input  [2:0] nzp,
  output out_4
);

  wire BEQ, BGE, BGT, BLE, BLT;

  _18BIT_COMPARATOR u_18bit_comparator_1 (.in_1(input1), .in_2(input2), .EQ(BEQ), .GT(BGT), .LT(BLT));
  or or_1 (BGE, BGT, BEQ);
  or or_2 (BLE, BEQ, BLT);
  Multiplexer #(.select(3)) multiplexer_1 (
    .in0(1'b0), .in1(BGT), .in2(BEQ), .in3(BGE), .in4(BLT), .in5(1'b0), .in6(BLE), .in7(1'b0), .out(out_4),
    .sel(nzp));  // open: en
endmodule

module Register_File_1 (
  input  Load,
  input  [19:0] in_2,
  input  Clk,
  input  [3:0] wr,
  input  [3:0] rd1,
  input  [3:0] rd2,
  output [19:0] outData1,
  output [19:0] outData2
);

  wire and_1_out, and_2_out, and_3_out, and_4_out, and_5_out, and_6_out, and_7_out, and_8_out, and_9_out,
       and_10_out, and_11_out, and_12_out, and_13_out, and_14_out, and_15_out, and_16_out, decoder_1_out0,
       decoder_1_out1, decoder_1_out2, decoder_1_out3, decoder_1_out4, decoder_1_out5, decoder_1_out6,
       decoder_1_out7, decoder_1_out8, decoder_1_out9, decoder_1_out10, decoder_1_out11, decoder_1_out12,
       decoder_1_out13, decoder_1_out14, decoder_1_out15, decoder_2_out0, decoder_2_out1, decoder_2_out2,
       decoder_2_out3, decoder_2_out4, decoder_2_out5, decoder_2_out6, decoder_2_out7, decoder_2_out8,
       decoder_2_out9, decoder_2_out10, decoder_2_out11, decoder_2_out12, decoder_2_out13, decoder_2_out14,
       decoder_2_out15, decoder_3_out0, decoder_3_out1, decoder_3_out2, decoder_3_out3, decoder_3_out4,
       decoder_3_out5, decoder_3_out6, decoder_3_out7, decoder_3_out8, decoder_3_out9, decoder_3_out10,
       decoder_3_out11, decoder_3_out12, decoder_3_out13, decoder_3_out14, decoder_3_out15;
  wire [19:0] R0_q, R1_q, R2_q, R3_q, R4_q, R5_q, R6_q, R7_q, R8_q, R9_q, R10_q, R11_q, R12_q, R13_q, R14_q,
       R15_q;

  Decoder #(.select(4), .enable("false")) decoder_1 (
    .out0(decoder_1_out0), .out1(decoder_1_out1), .out2(decoder_1_out2), .out3(decoder_1_out3),
    .out4(decoder_1_out4), .out5(decoder_1_out5), .out6(decoder_1_out6), .out7(decoder_1_out7),
    .out8(decoder_1_out8), .out9(decoder_1_out9), .out10(decoder_1_out10), .out11(decoder_1_out11),
    .out12(decoder_1_out12), .out13(decoder_1_out13), .out14(decoder_1_out14), .out15(decoder_1_out15),
    .sel(wr));
  and and_1 (and_1_out, Load, decoder_1_out0);
  and and_2 (and_2_out, Load, decoder_1_out1);
  and and_3 (and_3_out, Load, decoder_1_out2);
  and and_4 (and_4_out, Load, decoder_1_out3);
  and and_5 (and_5_out, Load, decoder_1_out4);
  and and_6 (and_6_out, Load, decoder_1_out5);
  and and_7 (and_7_out, Load, decoder_1_out6);
  and and_8 (and_8_out, Load, decoder_1_out7);
  Register #(.width(20)) R0 (.D(in_2), .en(and_1_out), .Q(R0_q), .clk(Clk), .clr(1'b0));
  Register #(.width(20)) R1 (.D(in_2), .en(and_2_out), .Q(R1_q), .clk(Clk), .clr(1'b0));
  Register #(.width(20)) R2 (.D(in_2), .en(and_3_out), .Q(R2_q), .clk(Clk), .clr(1'b0));
  Register #(.width(20)) R3 (.D(in_2), .en(and_4_out), .Q(R3_q), .clk(Clk), .clr(1'b0));
  Register #(.width(20)) R4 (.D(in_2), .en(and_5_out), .Q(R4_q), .clk(Clk), .clr(1'b0));
  Register #(.width(20)) R5 (.D(in_2), .en(and_6_out), .Q(R5_q), .clk(Clk), .clr(1'b0));
  Register #(.width(20)) R6 (.D(in_2), .en(and_7_out), .Q(R6_q), .clk(Clk), .clr(1'b0));
  Register #(.width(20)) R7 (.D(in_2), .en(and_8_out), .Q(R7_q), .clk(Clk), .clr(1'b0));
  and and_9 (and_9_out, Load, decoder_1_out8);
  and and_10 (and_10_out, Load, decoder_1_out9);
  and and_11 (and_11_out, Load, decoder_1_out10);
  and and_12 (and_12_out, Load, decoder_1_out11);
  and and_13 (and_13_out, Load, decoder_1_out12);
  and and_14 (and_14_out, Load, decoder_1_out13);
  and and_15 (and_15_out, Load, decoder_1_out14);
  and and_16 (and_16_out, Load, decoder_1_out15);
  Decoder #(.select(4), .enable("false")) decoder_2 (
    .out0(decoder_2_out0), .out1(decoder_2_out1), .out2(decoder_2_out2), .out3(decoder_2_out3),
    .out4(decoder_2_out4), .out5(decoder_2_out5), .out6(decoder_2_out6), .out7(decoder_2_out7),
    .out8(decoder_2_out8), .out9(decoder_2_out9), .out10(decoder_2_out10), .out11(decoder_2_out11),
    .out12(decoder_2_out12), .out13(decoder_2_out13), .out14(decoder_2_out14), .out15(decoder_2_out15),
    .sel(rd1));
  Decoder #(.select(4), .enable("false")) decoder_3 (
    .out0(decoder_3_out0), .out1(decoder_3_out1), .out2(decoder_3_out2), .out3(decoder_3_out3),
    .out4(decoder_3_out4), .out5(decoder_3_out5), .out6(decoder_3_out6), .out7(decoder_3_out7),
    .out8(decoder_3_out8), .out9(decoder_3_out9), .out10(decoder_3_out10), .out11(decoder_3_out11),
    .out12(decoder_3_out12), .out13(decoder_3_out13), .out14(decoder_3_out14), .out15(decoder_3_out15),
    .sel(rd2));
  Register #(.width(20)) R8 (.D(in_2), .en(and_9_out), .Q(R8_q), .clk(Clk), .clr(1'b0));
  Register #(.width(20)) R9 (.D(in_2), .en(and_10_out), .Q(R9_q), .clk(Clk), .clr(1'b0));
  Register #(.width(20)) R10 (.D(in_2), .en(and_11_out), .Q(R10_q), .clk(Clk), .clr(1'b0));
  Register #(.width(20)) R11 (.D(in_2), .en(and_12_out), .Q(R11_q), .clk(Clk), .clr(1'b0));
  Register #(.width(20)) R12 (.D(in_2), .en(and_13_out), .Q(R12_q), .clk(Clk), .clr(1'b0));
  Register #(.width(20)) R13 (.D(in_2), .en(and_14_out), .Q(R13_q), .clk(Clk), .clr(1'b0));
  Register #(.width(20)) R14 (.D(in_2), .en(and_15_out), .Q(R14_q), .clk(Clk), .clr(1'b0));
  Register #(.width(20)) R15 (.D(in_2), .en(and_16_out), .Q(R15_q), .clk(Clk), .clr(1'b0));
  assign outData1 = decoder_2_out0 ? R0_q : 20'bz;  // Controlled_Buffer controlled_buffer_1
  assign outData2 = decoder_3_out0 ? R0_q : 20'bz;  // Controlled_Buffer controlled_buffer_2
  assign outData1 = decoder_2_out1 ? R1_q : 20'bz;  // Controlled_Buffer controlled_buffer_3
  assign outData2 = decoder_3_out1 ? R1_q : 20'bz;  // Controlled_Buffer controlled_buffer_4
  assign outData1 = decoder_2_out2 ? R2_q : 20'bz;  // Controlled_Buffer controlled_buffer_5
  assign outData2 = decoder_3_out2 ? R2_q : 20'bz;  // Controlled_Buffer controlled_buffer_6
  assign outData1 = decoder_2_out3 ? R3_q : 20'bz;  // Controlled_Buffer controlled_buffer_7
  assign outData2 = decoder_3_out3 ? R3_q : 20'bz;  // Controlled_Buffer controlled_buffer_8
  assign outData1 = decoder_2_out4 ? R4_q : 20'bz;  // Controlled_Buffer controlled_buffer_9
  assign outData2 = decoder_3_out4 ? R4_q : 20'bz;  // Controlled_Buffer controlled_buffer_10
  assign outData1 = decoder_2_out5 ? R5_q : 20'bz;  // Controlled_Buffer controlled_buffer_11
  assign outData2 = decoder_3_out5 ? R5_q : 20'bz;  // Controlled_Buffer controlled_buffer_12
  assign outData1 = decoder_2_out6 ? R6_q : 20'bz;  // Controlled_Buffer controlled_buffer_13
  assign outData2 = decoder_3_out6 ? R6_q : 20'bz;  // Controlled_Buffer controlled_buffer_14
  assign outData1 = decoder_2_out7 ? R7_q : 20'bz;  // Controlled_Buffer controlled_buffer_15
  assign outData2 = decoder_3_out7 ? R7_q : 20'bz;  // Controlled_Buffer controlled_buffer_16
  assign outData1 = decoder_2_out8 ? R8_q : 20'bz;  // Controlled_Buffer controlled_buffer_17
  assign outData2 = decoder_3_out8 ? R8_q : 20'bz;  // Controlled_Buffer controlled_buffer_18
  assign outData1 = decoder_2_out9 ? R9_q : 20'bz;  // Controlled_Buffer controlled_buffer_19
  assign outData2 = decoder_3_out9 ? R9_q : 20'bz;  // Controlled_Buffer controlled_buffer_20
  assign outData1 = decoder_2_out10 ? R10_q : 20'bz;  // Controlled_Buffer controlled_buffer_21
  assign outData2 = decoder_3_out10 ? R10_q : 20'bz;  // Controlled_Buffer controlled_buffer_22
  assign outData1 = decoder_2_out11 ? R11_q : 20'bz;  // Controlled_Buffer controlled_buffer_23
  assign outData2 = decoder_3_out11 ? R11_q : 20'bz;  // Controlled_Buffer controlled_buffer_24
  assign outData1 = decoder_2_out12 ? R12_q : 20'bz;  // Controlled_Buffer controlled_buffer_25
  assign outData2 = decoder_3_out12 ? R12_q : 20'bz;  // Controlled_Buffer controlled_buffer_26
  assign outData1 = decoder_2_out13 ? R13_q : 20'bz;  // Controlled_Buffer controlled_buffer_27
  assign outData2 = decoder_3_out13 ? R13_q : 20'bz;  // Controlled_Buffer controlled_buffer_28
  assign outData1 = decoder_2_out14 ? R14_q : 20'bz;  // Controlled_Buffer controlled_buffer_29
  assign outData2 = decoder_3_out14 ? R14_q : 20'bz;  // Controlled_Buffer controlled_buffer_30
  assign outData1 = decoder_2_out15 ? R15_q : 20'bz;  // Controlled_Buffer controlled_buffer_31
  assign outData2 = decoder_3_out15 ? R15_q : 20'bz;  // Controlled_Buffer controlled_buffer_32
endmodule

module ALU_1 (
  input  [19:0] Input_1,
  input  [19:0] Input_2,
  input  [2:0] ALU_Controller,
  output [19:0] ALU_Out
);

  wire not_1_out;
  wire [19:0] Add_Sub_sum, and_1_out, or_1_out, xor_1_out;

  not not_1 (not_1_out, ALU_Controller[1]);
  assign and_1_out = Input_1 & Input_2;  // AND_Gate and_1, 20 bits wide
  Adder___20_Bits Add_Sub (
    .Input_1(Input_1), .sub_1_add_0(not_1_out), .Input_2(Input_2), .SUM(Add_Sub_sum));  // open: Overflow
  assign or_1_out = Input_1 | Input_2;  // OR_Gate or_1, 20 bits wide
  assign xor_1_out = Input_1 ^ Input_2;  // XOR_Gate xor_1, 20 bits wide
  Multiplexer #(.select(3), .width(20), .enable("false")) multiplexer_1 (
    .in0(and_1_out), .in1(Add_Sub_sum), .in2(or_1_out), .in3(Add_Sub_sum), .in4(xor_1_out), .out(ALU_Out),
    .sel(ALU_Controller));  // open: in5, in6, in7
endmodule

module Instruction_Parser_1 (
  input  [19:0] Instruction,
  output [19:0] Address3,
  output [3:0] SR2,
  output Z,
  output [2:0] ALU_Bits,
  output [3:0] Destination_Register,
  output [11:0] Address12,
  output [3:0] Source_Register,
  output [3:0] SR1,
  output [19:0] Imm
);

  assign Address3 = {{13{Instruction[7]}}, Instruction[7:1]};  // Bit_Extender bit_extender_1
  assign Imm = {{12{Instruction[7]}}, Instruction[7:0]};  // Bit_Extender bit_extender_2

  assign Address12 = Instruction[11:0];
  assign ALU_Bits = Instruction[19:17];
  assign Destination_Register = Instruction[15:12];
  assign Source_Register = Instruction[15:12];
  assign SR1 = Instruction[11:8];
  assign SR2 = Instruction[7:4];
  assign Z = Instruction[0];

  // Other names for the same wires on the sheet: Opcode[3:0] = Instruction[19:16]
endmodule

module Program_Counter_1 (
  input  [19:0] JUMP_ADDRESS,
  input  in_2,
  input  Clear,
  input  Enable,
  input  Clock,
  input  ADDRSelect,
  output [19:0] PC_address
);

  wire [19:0] adder_20_bits_1_sum, multiplexer_1_out, multiplexer_2_out;

  Multiplexer #(.width(20)) multiplexer_1 (
    .in0(20'h1), .in1(JUMP_ADDRESS), .out(multiplexer_1_out), .sel(ADDRSelect));  // open: en
  Adder___20_Bits adder_20_bits_1 (
    .Input_1(multiplexer_1_out), .sub_1_add_0(in_2), .Input_2(multiplexer_2_out), .SUM(adder_20_bits_1_sum));  // open: Overflow
  Multiplexer #(.width(20)) multiplexer_2 (
    .in0(PC_address), .in1({20{1'b0}}), .out(multiplexer_2_out), .sel(ADDRSelect));  // open: en
  Register #(.width(20), .trigger("falling")) register_1 (
    .D(adder_20_bits_1_sum), .en(Enable), .Q(PC_address), .clk(Clock), .clr(Clear));
endmodule

module Sign_Extend_Value_1 (
  input  [19:0] Input,
  output [19:0] Output
);


  assign Output = {{5{Input[15]}}, Input[14:0]};
endmodule

module Branch_Signal_1 (
  input  [19:0] input1,
  input  [19:0] input2,
  input  nzp,
  output out_4
);

  wire n20bit_comparator_1_1_eq, not_1_out;

  _20Bit_Comparator_1 u_20bit_comparator_1_1 (.in_1(input1), .in_2(input2), .EQ(n20bit_comparator_1_1_eq));
  not not_1 (not_1_out, n20bit_comparator_1_1_eq);
  Multiplexer #(.enable("false")) multiplexer_1 (
    .in0(not_1_out), .in1(n20bit_comparator_1_1_eq), .out(out_4), .sel(nzp));
endmodule
